# Fritzing sketch Placa (saved by Fritzing 0.9.3b)

parts:
  U1 = ESP32-WROOM-32D-NodeMCU
  M1 = Getriebemotor
  M2 = Getriebemotor
  L298N1 = L298N DC motor driver
  HC-SR04_Sensor_1 = HC-SR04 Ultrasonic Distance Sensor
  HC-SR04_Sensor_2 = HC-SR04 Ultrasonic Distance Sensor
  ESP32_-_Front1 = ESP32 - CAM  # not connected
  J1 = Basic Servo  # not connected
  KY-1 = Keyes Photo Resistor Sensor [package=THT]
  VCC1 = Battery  # not connected

nets:
  N1: U1.3.3V, KY-1.power
  N2: U1.G35, KY-1.signal
  N3: U1.G26, L298N1.IN1
  N4: U1.G27, L298N1.IN2
  N5: U1.G14, L298N1.IN3
  N6: U1.G12, L298N1.IN4
  N7: U1.GND#13, KY-1.ground
  5V: U1.5V, L298N1.5V, HC-SR04_Sensor_1.VCC
  N8: U1.G15, L298N1.ENB
  N9: U1.G2, L298N1.ENA
  N10: U1.G16, HC-SR04_Sensor_2.ECHO
  N11: U1.G17, HC-SR04_Sensor_2.TRIG
  N12: U1.G5, HC-SR04_Sensor_1.TRIG
  N13: U1.G18, HC-SR04_Sensor_1.ECHO
  GND: U1.GND#50, L298N1.GND, HC-SR04_Sensor_1.GND, HC-SR04_Sensor_2.GND
  N14: M1.pin_1, L298N1.OUT1
  N15: M2.pin_1, L298N1.OUT3

custom parts:
  L298N DC motor driver: 2x DC motor driver with 78M05 positive voltage regulator (7..35 V) L298N: max 46 V, 2 A Set 5 V Enable jumper to enable 5 V regultor (needed for the L298N) and +5 V output at screw terminal or supply external +5 V at screw terminal Set ENA and/or ENB to +5 V to enable motor permanently or supply ENA and/or ENB with PWM signal IN1 and IN2 set rotation directory for motor A (OUT1/OUT2) IN2 and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
  ESP32 - CAM: The ESP32-CAM has a very competitive small-size camera module that can operate independently as a minimum system with a footprint of only 27*40.5*4.5mm and a deep sleep current of up to 6mA.
  Keyes Photo Resistor Sensor: Keyes Photo Resistor Sensor Module for Arduino.
  Battery: Your standard 2x 18650 battery pack (7,4 Volts)
